# Fritzing sketch testbedUartMode (saved by Fritzing 1.0.6)
circuit board: 8.46667cm x 5.64444cm
breadboards: 1

parts:
  Microcontroller = Arduino Mega 2560 (Rev3)
  PSU = Hanmatek HM305
  M1 = Stepper Motor - Bipolar
  R1 = Resistor [tolerance=±5% power=0.25W resistance=220k package=THT]
  R2 = Resistor [tolerance=±5% power=0.25W resistance=47k package=THT]
  Mod2 = TMC2209 [package=THT]
  C1 = Electrolytic Capacitor [capacitance=47µF voltage=50V package="200 mil [THT, electrolytic]"]
  R3 = Resistor [tolerance=±5% power=0.25W resistance=1k package=THT]

nets:
  N1: Microcontroller.A0, R1.Pin_1, R2.Pin_1
  N2: Microcontroller.D19/RX1, Mod2.PDN
  N3: Microcontroller.D18/TX1, R3.Pin_0
  N4: Microcontroller.5V, Mod2.VIO
  GND: Microcontroller.GND, PSU.Pin_3, R2.Pin_0, Mod2.GND, Mod2.MS1, Mod2.MS2, Mod2.EN, C1.-
  N5: Microcontroller.D2_PWM, Mod2.Dir
  N6: Microcontroller.D3_PWM, Mod2.Step
  N7: PSU.Pin_4, R1.Pin_0, Mod2.VM, C1.+
  N8: M1.A, Mod2.M1B
  N9: M1.C, Mod2.M1A
  N10: M1.B, Mod2.M2A
  N11: M1.D, Mod2.M2B
  N12: Mod2.UART, R3.Pin_1

custom parts:
  Hanmatek HM305: DC Power Supply 30V5A HM305.
  TMC2209: TMC2209-LA stepper motor controller and driver. Supply voltage 4.75-28V Iphase up to 1.77A rms (2.5A peak)
